# Fritzing sketch slider (saved by Fritzing 0.9.3b)

parts:
  Часть1 = Arduino Nano (Rev3.0)
  Pololu_A1 = Pololu A4988 [package=SO16]
  S1 = Limit Switch [package="Breakout Board"]
  F1 = FUSE [package=fuse_5mm]
  R1 = Rotary Potentiometer (Small) [maximum_resistance=50kΩ package=THT]
  C1 = Ceramic Capacitor [capacitance=100nF package="100 mil [THT, multilayer]"]
  C2 = Electrolytic Capacitor [capacitance=47µF package="100 mil [THT, electrolytic]"]
  M1 = Stepper Motor - Unipolar
  BAT2 = Battery Holders [package=lipo-1100mAh]

nets:
  GND: Часть1.GND, Pololu_A1.GND, S1.G, R1.leg2, C1.0, C2.-, BAT2.-
  N1: Часть1.D7, S1.S
  N2: Часть1.D8, Pololu_A1.DIR
  N3: Часть1.D9, Pololu_A1.STEP
  N4: Часть1.VIN, Pololu_A1.VMOT, F1.2, C2.+
  5V: Часть1.5V, Pololu_A1.MS1, Pololu_A1.MS2, Pololu_A1.MS3, Pololu_A1.VDD, S1.V, R1.leg1
  N5: Часть1.A0, R1.wiper, C1.1
  N6: Pololu_A1.RESET, Pololu_A1.SLEEP
  N7: Pololu_A1.1B, M1.D
  N8: Pololu_A1.1A, M1.B
  N9: Pololu_A1.2A, M1.C
  N10: Pololu_A1.2B, M1.A
  N11: F1.1, BAT2.+

custom parts:
  Limit Switch: Generic limit switch commonly found on 3D printers. Typical lever microswitch mounted on a PCB board with a 3 pin JST XH connector.
