# Fritzing sketch slider_5V (saved by Fritzing 0.9.3b)

parts:
  Часть1 = Arduino Nano (Rev3.0)
  Pololu_A1 = Pololu A4988 [package=SO16]
  S1 = Limit Switch [package="Breakout Board"]
  R1 = Rotary Potentiometer (Small) [maximum_resistance=50kΩ package=THT]
  C1 = Ceramic Capacitor [capacitance=100nF package="100 mil [THT, multilayer]"]
  C2 = Electrolytic Capacitor [capacitance=47µF package="100 mil [THT, electrolytic]"]
  M1 = Stepper Motor - Unipolar
  BAT2 = Battery Holders [package=lipo-1100mAh]
  M3 = MT3608 Module

nets:
  GND: Часть1.GND, Pololu_A1.GND, S1.G, R1.leg2, C1.0, C2.-, BAT2.-, M3.pin1, M3.pin4
  N1: Часть1.D7, S1.S
  N2: Часть1.D8, Pololu_A1.DIR
  N3: Часть1.D9, Pololu_A1.STEP
  5V: Часть1.5V, Pololu_A1.MS1, Pololu_A1.MS2, Pololu_A1.MS3, Pololu_A1.VDD, S1.V, R1.leg1, BAT2.+, M3.pin2
  N4: Часть1.A0, R1.wiper, C1.1
  N5: Pololu_A1.RESET, Pololu_A1.SLEEP
  N6: Pololu_A1.1B, M1.D
  N7: Pololu_A1.1A, M1.B
  N8: Pololu_A1.2A, M1.C
  N9: Pololu_A1.2B, M1.A
  N10: Pololu_A1.VMOT, C2.+, M3.pin3

custom parts:
  Limit Switch: Generic limit switch commonly found on 3D printers. Typical lever microswitch mounted on a PCB board with a 3 pin JST XH connector.
  MT3608 Module: MT3608 Boost Converter Module Links: Aerosemi MT3608 2A Step Up Converter datasheet
